// Digital circuit 555 timer.dig as structural Verilog
module _555_timer (
  input  _555_Timer,
  output out_2,
  output out_3,
  output out_4,
  output out_5,
  output out_6,
  output out_7,
  output out_8,
  output out_9,
  output out_10,
  output out_11,
  output out_12,
  output out_13,
  output out_14,
  output out_15,
  output out_16,
  output out_17,
  output out_18,
  output out_19,
  output out_20,
  output out_21,
  output out_22,
  output out_23,
  output out_24
);

  wire _7400_1_pin6, _7400_2_pin3, _7404_1_pin1, _7404_1_pin2, _7404_1_pin3, _7404_1_pin4, _7404_1_pin10,
       _7404_1_pin12, _7447_1_pin9, _7447_1_pin10, _7447_1_pin11, _7447_1_pin12, _7447_1_pin13,
       _7447_1_pin14, _7447_1_pin15, _7447_2_pin9, _7447_2_pin10, _7447_2_pin11, _7447_2_pin12,
       _7447_2_pin13, _7447_2_pin14, _7447_2_pin15, _7447_3_pin9, _7447_3_pin10, _7447_3_pin11,
       _7447_3_pin12, _7447_3_pin13, _7447_3_pin14, _7447_3_pin15, _74162_2_pin7;

  _7400 _7400_1 (
    .pin1(1'b0), .pin2(1'b0), .pin4(out_17), .pin5(out_17), .pin6(_7400_1_pin6), .pin7(1'b0), .pin8(out_22),
    .pin9(_7400_1_pin6), .pin10(_7400_1_pin6), .pin12(1'b0), .pin13(1'b0), .pin14(1'b1));  // open: pin3, pin11
  _7404 _7404_1 (
    .pin1(_7404_1_pin1), .pin2(_7404_1_pin2), .pin3(_7404_1_pin3), .pin4(_7404_1_pin4), .pin5(1'b0),
    .pin7(1'b0), .pin9(1'b0), .pin10(_7404_1_pin10), .pin11(out_4), .pin12(_7404_1_pin12), .pin13(out_2),
    .pin14(1'b1));  // open: pin6, pin8
  _7447 _7447_1 (
    .pin1(out_16), .pin2(out_15), .pin3(1'b1), .pin4(1'b1), .pin5(1'b1), .pin6(out_14), .pin7(out_17),
    .pin8(1'b0), .pin9(_7447_1_pin9), .pin10(_7447_1_pin10), .pin11(_7447_1_pin11), .pin12(_7447_1_pin12),
    .pin13(_7447_1_pin13), .pin14(_7447_1_pin14), .pin15(_7447_1_pin15), .pin16(1'b1));
  _74162 _74162_1 (
    .pin1(1'b1), .pin2(_7400_1_pin6), .pin3(1'b0), .pin4(1'b0), .pin5(1'b0), .pin6(1'b0), .pin7(out_23),
    .pin8(1'b0), .pin9(1'b1), .pin10(1'b1), .pin11(out_21), .pin12(out_20), .pin13(out_19), .pin14(out_18),
    .pin16(1'b1));  // open: pin15
  _7400 _7400_2 (
    .pin1(_7404_1_pin2), .pin2(_7404_1_pin4), .pin3(_7400_2_pin3), .pin4(1'b0), .pin5(1'b0), .pin7(1'b0),
    .pin8(_7404_1_pin1), .pin9(out_5), .pin10(_7404_1_pin10), .pin11(_7404_1_pin3), .pin12(out_3),
    .pin13(_7404_1_pin12), .pin14(1'b1));  // open: pin6
  _7447 _7447_2 (
    .pin1(out_19), .pin2(out_20), .pin3(1'b1), .pin4(1'b1), .pin5(1'b1), .pin6(out_21), .pin7(out_18),
    .pin8(1'b0), .pin9(_7447_2_pin9), .pin10(_7447_2_pin10), .pin11(_7447_2_pin11), .pin12(_7447_2_pin12),
    .pin13(_7447_2_pin13), .pin14(_7447_2_pin14), .pin15(_7447_2_pin15), .pin16(1'b1));
  _74161 _74161_1 (
    .pin1(_7400_2_pin3), .pin2(_555_Timer), .pin3(1'b0), .pin4(1'b0), .pin5(1'b0), .pin6(1'b0), .pin7(1'b1),
    .pin8(1'b0), .pin9(1'b1), .pin10(1'b1), .pin11(out_5), .pin12(out_4), .pin13(out_3), .pin14(out_2),
    .pin16(1'b1));  // open: pin15
  Seven_Seg #(.commonCathode("true"), .commonConnectionType("anode")) seven_seg_1 (
    .a(_7447_2_pin13), .b(_7447_2_pin12), .c(_7447_2_pin11), .d(_7447_2_pin10), .e(_7447_2_pin9),
    .f(_7447_2_pin15), .g(_7447_2_pin14), .dp(1'b0), .common(1'b1));
  Seven_Seg #(.commonCathode("true"), .commonConnectionType("anode")) seven_seg_2 (
    .a(_7447_1_pin13), .b(_7447_1_pin12), .c(_7447_1_pin11), .d(_7447_1_pin10), .e(_7447_1_pin9),
    .f(_7447_1_pin15), .g(_7447_1_pin14), .dp(1'b0), .common(1'b1));
  _74162 _74162_2 (
    .pin1(1'b1), .pin2(_555_Timer), .pin3(1'b0), .pin4(1'b0), .pin5(1'b0), .pin6(1'b0), .pin7(_74162_2_pin7),
    .pin8(1'b0), .pin9(1'b1), .pin10(1'b1), .pin11(out_14), .pin12(out_15), .pin13(out_16), .pin14(out_17),
    .pin15(out_23), .pin16(1'b1));
  Seven_Seg #(.commonConnectionType("anode"), .commonCathode("true")) seven_seg_3 (
    .a(_7447_3_pin13), .b(_7447_3_pin12), .c(_7447_3_pin11), .d(_7447_3_pin10), .e(_7447_3_pin9),
    .f(_7447_3_pin15), .g(_7447_3_pin14), .dp(1'b0), .common(1'b1));
  _7447 _7447_3 (
    .pin1(out_11), .pin2(out_12), .pin3(1'b1), .pin4(1'b1), .pin5(1'b1), .pin6(out_13), .pin7(out_10),
    .pin8(1'b0), .pin9(_7447_3_pin9), .pin10(_7447_3_pin10), .pin11(_7447_3_pin11), .pin12(_7447_3_pin12),
    .pin13(_7447_3_pin13), .pin14(_7447_3_pin14), .pin15(_7447_3_pin15), .pin16(1'b1));
  _74161 _74161_2 (
    .pin1(1'b1), .pin2(_555_Timer), .pin3(1'b0), .pin4(1'b0), .pin5(1'b0), .pin6(1'b0), .pin7(1'b1),
    .pin8(1'b0), .pin9(1'b1), .pin10(1'b1), .pin11(out_9), .pin12(out_8), .pin13(out_7), .pin14(out_6),
    .pin16(1'b1));  // open: pin15
  _74162 _74162_3 (
    .pin1(1'b1), .pin2(_555_Timer), .pin3(1'b0), .pin4(1'b0), .pin5(1'b0), .pin6(1'b0), .pin7(1'b1),
    .pin8(1'b0), .pin9(1'b1), .pin10(1'b1), .pin11(out_13), .pin12(out_12), .pin13(out_11), .pin14(out_10),
    .pin15(_74162_2_pin7), .pin16(1'b1));

  assign out_24 = _555_Timer;
endmodule
